# Fritzing sketch arduinobluetootharaba (saved by Fritzing 0.9.3b)
perfboards: 1

parts:
  Parça1 = Arduino Uno (Rev3)
  M1 = DC Motor
  R1 = Resistor [tolerance=±5% resistance=1 package=THT]
  Parça2 = Bluetooth HC-05 Macho
  R2 = Resistor [tolerance=±5% resistance=1 package=THT]
  U1 = L298 [package=multiwatt15]
  VCC1 = Battery block 9V
  LED1 = LED - 5mm [color="Red (633nm)" package="5 mm [THT]"]  # not connected
  LED2 = LED - 5mm [color="Red (633nm)" package="5 mm [THT]"]
  R4 = Resistor [tolerance=±5% resistance=220 package=THT]
  R6 = Resistor [tolerance=±5% resistance=1 package=THT]
  J2 = Piezo Speaker
  hc-sr1 = hc-sr04
  J1 = Basic Servo
  R7 = Resistor [tolerance=±5% resistance=220 package=THT]  # not connected
  LED3 = LED - 5mm [color="Red (633nm)" package="5 mm [THT]"]
  LED4 = LED - 5mm [color="Red (633nm)" package="5 mm [THT]"]  # not connected
  VCC2 = Battery block 9V  # not connected

nets:
  N1: Parça1.D8, LED3.anode
  N2: Parça1.D9_PWM, J2.pin2
  N3: Parça1.D10_PWM/SS, U1.IN4
  N4: Parça1.D11_PWM/MOSI, U1.IN3
  GND: Parça1.GND, Parça2.GND, J1.gnd
  N5: Parça1.D0/RX, Parça2.TXD
  N6: Parça1.D2, hc-sr1.Trig
  N7: Parça1.D3_PWM, hc-sr1.Echo
  N8: Parça1.D5_PWM, J1.pulse
  N9: Parça1.D7, LED2.anode
  3V3: Parça1.3V3, Parça2.VCC
  VCC: Parça1.5V, hc-sr1.VCC, J1.vcc
  N10: M1.pin_1, U1.OUT3
  N11: M1.pin_2, U1.OUT4
  N12: R1.Pin_0, R6.Pin_1
  N13: R1.Pin_1, Parça2.RXD, R2.Pin_0
  N14: U1.GND, R4.Pin_0
  N15: U1.VLS, VCC1.+

// code stored in the sketch: bluetootharaba.ino
#include <SoftwareSerial.h> // Bluetooth için seri ileti?im kütüphanesi
#include <Servo.h>          // Servo motor için kütüphane



SoftwareSerial bt_iletisim(0, 1); //  Bluetooth s?ras?yla RX | TX pinlerini tan?t?yoruz
Servo servoMotor;


//Kullan?lan program = ControlJoystick veya Arduino Car


//I?IKLANDIRMA
const int onFar         = 8 ;// ÖN FAR P?N
const int arkaStop      = 7 ;// ARKA STOP P?N


//Buzzer
const int buzzer        = 6;//Buzzer Pin


//Mesafe Sensörü
const int mesafeSensoruEcho = 3;
const int mesafeSensoruTrig = 2;
long sure;
double mesafe;


//MOTOR P?NLER?
const int out3          = 10;
const int out4          = 11;
//const int hizKontrol    = A0 ;


//FONS?YONLARIN ÖN TANIMLANMASI
void motorIleri();
void motorGeri();


void servoSagaDondur();
void servoSolaDondur();
void servoOrtala();


void mesafeOlc();
void mesafeKontrol();


void onFarYak();
void arkaStopYak();
void dortluYak();


void kornaCal();



char komut;//Bluetooth ile gelen komut



void setup()
{
  Serial.begin(9600);
 
  //BLUETOOTH SETUP
  bt_iletisim.begin(9600);
  
  //SERVO Setup
  servoMotor.attach(5);


  //Mesafe Sensörü Setup
  pinMode(mesafeSensoruTrig, OUTPUT);
  pinMode(mesafeSensoruEcho, INPUT);


  //I?IKLANDIRMA P?N TANITIMI
  pinMode(onFar, OUTPUT);
  pinMode(arkaStop, OUTPUT);


  //Buzzer Tan?t?m?
  pinMode(buzzer, OUTPUT);


  //MOTOR P?N TANITIMI
  pinMode(out3, OUTPUT);
  pinMode(out4, OUTPUT);
  //pinMode(hizKontrol,OUTPUT);
  
    
}


void loop()
{
  //mesafeOlc();
  //mesafeKontrol();
  if (Serial.available() > 0)
  {
    komut = Serial.read();
    Serial.println(komut);
        
    //MOTOR KONTROLLER?
    if (komut == 'F')
    {
      motorIleri();
      servoOrtala();
    }
    if (komut == 'B')
    {
      motorGeri();
      servoOrtala();
    }
    if (komut == 'S' || komut == 'D')
    {
      motorDur();
      servoOrtala();
    }
    //SERVO KONTROLLER?
    if (komut == 'L')
    {
      servoSolaDondur();
      motorDur();
    }
    if (komut == 'R')
    {
      servoSagaDondur();
      motorDur();
    }
    //ORTA YÖNLER
    if (komut == 'G')
    {
      servoSolaDondur();
      motorIleri();
    }
    if (komut == 'I')
    {
      servoSagaDondur();
      motorIleri();
    }
    if (komut == 'H')
    {
      servoSolaDondur();
      motorGeri();
    }
    if (komut == 'J')
    {
      servoSagaDondur();
      motorGeri();
    }
    //KORNA
    if (komut == 'V' || komut == 'v')
    {
      kornaCal();
    }
    //FAR KONTROLLER?
    if (komut == 'W' || komut == 'w')
    {
      onFarYak();
    }
    if (komut == 'U' || komut == 'u')
    {
      arkaStopYak();
    }
    if (komut == 'X' || komut == 'x')
    {
      Serial.println("BO? KOD");
      //dortluYak();
    }
  }
  else
  {
    motorDur();
    servoOrtala();
  }
}
// #########################   MOTOR FONKS?YONLARI  ####################
// #  H?z aral??? 99-255
void motorIleri()
{
  digitalWrite(out3, HIGH);
  digitalWrite(out4, LOW);
  //analogWrite(hizKontrol,200);


}
void motorGeri()
{
  digitalWrite(out3, LOW);
  digitalWrite(out4, HIGH);
  //analogWrite(hizKontrol,200);
}
void motorDur()
{
  digitalWrite(out3, HIGH);
  digitalWrite(out4, HIGH);


}


// #########################   SERVO FONKS?YONLARI  ########################
//SERVO D?REKS?YON ARALIKLARI (minimum:77 maksimum:99 orta:88)


void servoSagaDondur()
{
  servoMotor.write(99);
}
void servoSolaDondur()
{
  servoMotor.write(77);
}
void servoOrtala()
{
  servoMotor.write(88);
}


// ######################### I?IKLANDIRMA FONKS?YONLARI #####################


void onFarYak()
{
  digitalWrite(onFar, !digitalRead(onFar)); // ÖN FAR YAK - SONDUR
}
void arkaStopYak()
{
  digitalWrite(arkaStop, !digitalRead(arkaStop)); // ARKA STOP YAK -SONDUR
}
void dortluYak()
{
  digitalWrite(arkaStop, !digitalRead(arkaStop));
  delay(500);
  digitalWrite(arkaStop, !digitalRead(arkaStop));
  delay(500);


}


// ######################### BUZZER FONKS?YONLARI ####################


void kornaCal()
{
  digitalWrite(buzzer, !digitalRead(buzzer));


}


// #################### MESAFE FONKS?YONLARI ########################


void mesafeOlc()
{
  digitalWrite(mesafeSensoruTrig, HIGH);  
  delayMicroseconds(1000);
  digitalWrite(mesafeSensoruTrig, LOW);


  sure = pulseIn(mesafeSensoruEcho, HIGH);
  //Gidi? geli? oldu?u için geçen süreyi ikiye bölüyoruz ve 
  // sonucunuda ses h?z?na bölüyoruz(ses hizi=343 m/s)
  mesafe = (sure/2) / 29.1;


  Serial.print("Mesafe=");
  Serial.println(mesafe);


}
void mesafeKontrol()
{
  if(mesafe<10)
  {
    motorGeri();
    delay(50);
    motorDur();
  }   
}
